// Logisim project kan_32bit_ALU.circ as structural Verilog: 1 circuit, main circuit main
module main (
  input  [31:0] in_1,
  input  [31:0] in_2,
  input  [1:0] in_3,
  output [31:0] out_4,
  output Zero,
  output Negative,
  output Overflow,
  output Carry
);

  wire or_2_out, or_3_out, subtractor_1_bout;
  wire [31:0] adder_1_out, and_1_out, or_1_out, subtractor_1_out;

  assign and_1_out = in_1 & in_2;  // AND_Gate and_1, 32 bits wide
  assign or_1_out = in_1 | in_2;  // OR_Gate or_1, 32 bits wide
  Adder #(.width(32)) adder_1 (.a(in_1), .b(in_2), .out(adder_1_out), .cout(Carry));  // open: cin
  Subtractor #(.width(32)) subtractor_1 (
    .a(in_1), .b(in_2), .out(subtractor_1_out), .bout(subtractor_1_bout));  // open: bin
  or or_2 (or_2_out, Carry, subtractor_1_bout);
  not not_1 (Zero, or_3_out);
  and and_2 (Overflow, in_3[1], or_2_out);
  or or_3 (or_3_out, Negative, out_4[30], out_4[29], out_4[28], out_4[27], out_4[26], out_4[25], out_4[24], out_4[23], out_4[22], out_4[21], out_4[20], out_4[19], out_4[18], out_4[17], out_4[16], out_4[15], out_4[13], out_4[12], out_4[11], out_4[10], out_4[9], out_4[8], out_4[7], out_4[6], out_4[5], out_4[4], out_4[3], out_4[2], out_4[1], out_4[0], out_4[14]);
  Multiplexer #(.select(2), .width(32), .enable("false")) multiplexer_1 (
    .in0(and_1_out), .in1(or_1_out), .in2(adder_1_out), .in3(subtractor_1_out),
    .out({Negative, out_4[30:0]}), .sel(in_3));

  assign out_4[31] = Negative;

  // Notes on the sheet:
  //   Input 1
  //   Input 2
  //   Op code
  //   00 - bitwise AND
  //   01 - bitwise OR
  //   10 - Addition
  //   11 - Subtraction
  //   32-Bit ALU
  //   - a type of calculator in a processor that performs
  //   the operations corresponding to the set op-code
  //   Result
endmodule
