// Logisim project kan_8bit_register.circ as structural Verilog: 5 circuits, main circuit main
module main (
);


  // Notes on the sheet:
  //   Click Register8 on left-side
endmodule

module MemoryCell (
  input  Clock,
  input  InputEnable,
  input  Din,
  input  OutputEnable,
  input  Reset,
  output Dout,
  output StoredData
);

  wire and_1_out, and_2_out, not_1_out, or_1_out;

  not not_1 (not_1_out, InputEnable);
  and and_1 (and_1_out, StoredData, not_1_out);
  or or_1 (or_1_out, and_1_out, and_2_out);
  and and_2 (and_2_out, InputEnable, Din);
  D_Flip_Flop d_ff_1 (.D(or_1_out), .clk(Clock), .Q(StoredData), .reset(Reset));  // open: Qn, preset
  assign Dout = OutputEnable ? StoredData : 1'bz;  // Controlled_Buffer controlled_buffer_1
endmodule

module Register8 (
  input  Clock,
  input  InputEnable,
  input  [7:0] Din,
  input  OutputEnable,
  output [7:0] Dout,
  output [7:0] StoredData
);

  MemoryCell M0 (
    .Clock(Clock), .InputEnable(InputEnable), .Din(Din[0]), .OutputEnable(OutputEnable), .Dout(Dout[0]),
    .StoredData(StoredData[0]));  // open: Reset
  MemoryCell M1 (
    .Clock(Clock), .InputEnable(InputEnable), .Din(Din[1]), .OutputEnable(OutputEnable), .Dout(Dout[1]),
    .StoredData(StoredData[1]));  // open: Reset
  MemoryCell M2 (
    .Clock(Clock), .InputEnable(InputEnable), .Din(Din[2]), .OutputEnable(OutputEnable), .Dout(Dout[2]),
    .StoredData(StoredData[2]));  // open: Reset
  MemoryCell M3 (
    .Clock(Clock), .InputEnable(InputEnable), .Din(Din[3]), .OutputEnable(OutputEnable), .Dout(Dout[3]),
    .StoredData(StoredData[3]));  // open: Reset
  MemoryCell M4 (
    .Clock(Clock), .InputEnable(InputEnable), .Din(Din[4]), .OutputEnable(OutputEnable), .Dout(Dout[4]),
    .StoredData(StoredData[4]));  // open: Reset
  MemoryCell M5 (
    .Clock(Clock), .InputEnable(InputEnable), .Din(Din[5]), .OutputEnable(OutputEnable), .Dout(Dout[5]),
    .StoredData(StoredData[5]));  // open: Reset
  MemoryCell M6 (
    .Clock(Clock), .InputEnable(InputEnable), .Din(Din[6]), .OutputEnable(OutputEnable), .Dout(Dout[6]),
    .StoredData(StoredData[6]));  // open: Reset
  MemoryCell M7 (
    .Clock(Clock), .InputEnable(InputEnable), .Din(Din[7]), .OutputEnable(OutputEnable), .Dout(Dout[7]),
    .StoredData(StoredData[7]));  // open: Reset

  // Notes on the sheet:
  //   8 Bit Register
  //   InputEnable must be set to 1 to read the input
  //   Clock Ticks can be set by: Click 'Simulate', Set 'Ticks Enabled'
  //   OutputEnable shows the output in Dout but the output will always be shown in StoredOutput at the clock's rising edge
endmodule

module MAR (
  input  Clock,
  input  InputEnable,
  input  [3:0] Din,
  input  OutputEnable,
  output [3:0] Dout,
  output [3:0] StoredOutput
);

  MemoryCell memorycell_1 (
    .Clock(Clock), .InputEnable(InputEnable), .Din(Din[0]), .OutputEnable(OutputEnable), .Dout(Dout[0]),
    .StoredData(StoredOutput[0]));  // open: Reset
  MemoryCell memorycell_2 (
    .Clock(Clock), .InputEnable(InputEnable), .Din(Din[1]), .OutputEnable(OutputEnable), .Dout(Dout[1]),
    .StoredData(StoredOutput[1]));  // open: Reset
  MemoryCell memorycell_3 (
    .Clock(Clock), .InputEnable(InputEnable), .Din(Din[2]), .OutputEnable(OutputEnable), .Dout(Dout[2]),
    .StoredData(StoredOutput[2]));  // open: Reset
  MemoryCell memorycell_4 (
    .Clock(Clock), .InputEnable(InputEnable), .Din(Din[3]), .OutputEnable(OutputEnable), .Dout(Dout[3]),
    .StoredData(StoredOutput[3]));  // open: Reset

  // Notes on the sheet:
  //   4 Bit Memory Address Register
endmodule

module simpleALU (
  input  [7:0] RegA,
  input  [7:0] RegB,
  input  OutputEnable,
  output [7:0] Dout,
  output [7:0] ALU_Result,
  output CarryOut
);

  Adder adder_1 (.a(RegA), .b(RegB), .out(ALU_Result), .cout(CarryOut));  // open: cin
  assign Dout = OutputEnable ? ALU_Result : 8'bz;  // Controlled_Buffer controlled_buffer_1

  // Notes on the sheet:
  //   Simple 8-Bit ALU
endmodule
