// Logisim project kan_bitmem.circ as structural Verilog: 1 circuit, main circuit main
module main (
  input  InputEnable,
  input  Din,
  input  OutputEnable,
  input  Reset,
  output Dout,
  output StoredOutput
);

  wire and_1_out, and_2_out, clock_1_out, not_1_out, or_1_out;

  not not_1 (not_1_out, InputEnable);
  and and_1 (and_1_out, StoredOutput, not_1_out);
  or or_1 (or_1_out, and_1_out, and_2_out);
  and and_2 (and_2_out, InputEnable, Din);
  Clock clock_1 (.out(clock_1_out));
  D_Flip_Flop d_ff_1 (.D(or_1_out), .clk(clock_1_out), .Q(StoredOutput), .reset(Reset));  // open: Qn, preset
  assign Dout = OutputEnable ? StoredOutput : 1'bz;  // Controlled_Buffer controlled_buffer_1

  // Notes on the sheet:
  //   InputEnable must be set to 1 to read the input
  //   Clock Ticks can be set by: Click 'Simulate', Set 'Ticks Enabled'
  //   Memory Cell
  //   (using D-Flip-Flops)
  //   OutputEnable shows the output in Dout but the output will always be shown in StoredOutput at the clock's rising edge
endmodule
