// Logisim project kan_full_adder.circ as structural Verilog: 1 circuit, main circuit main
module main (
  input  Carryin0,
  input  A0,
  input  B0,
  input  Carryin1,
  input  A1,
  input  B1,
  output Result0,
  output Carryout0,
  output Result1,
  output Carryout1
);

  wire and_1_out, and_2_out, xor_1_out;

  and and_1 (and_1_out, A1, B1);
  Adder #(.width(1)) adder_1 (.a(A0), .b(B0), .out(Result0), .cin(Carryin0), .cout(Carryout0));
  xor xor_1 (xor_1_out, A1, B1);
  or or_1 (Carryout1, and_1_out, and_2_out);
  and and_2 (and_2_out, Carryin1, xor_1_out);
  xor xor_2 (Result1, Carryin1, xor_1_out);

  // Notes on the sheet:
  //   Logisim built-in full adder
  //   My implementation of full adder
  //   using wires and gates
  //   - Performs binary addition
  //   multiple-bit full adders
  //   Full Adder
  //   - A, B are input values can be 0 or 1
  //   - Carry in bit can be used to connect 
  //   with another full adder to create
endmodule
