// Logisim project kan_latches.circ as structural Verilog: 1 circuit, main circuit main
module main (
  input  in_1,
  input  Enable,
  input  Input,
  input  Input_2,
  input  Enable_2,
  input  Input_3,
  output Output,
  output out_8,
  output Output_2,
  output Output_3,
  output Inverted_Output
);

  wire and_1_out, and_2_out, and_3_out, and_4_out, and_5_out, and_6_out, button_1_out, clock_1_out,
       nor_4_out, nor_6_out, not_1_out, not_2_out, not_3_out, not_4_out, not_5_out;

  Button button_1 (.out(button_1_out));
  or or_1 (out_8, in_1, out_8);
  nor nor_1 (Output_2, button_1_out, Inverted_Output);
  nor nor_2 (Inverted_Output, Output_2, Input_2);
  Clock clock_1 (.out(clock_1_out));
  not not_1 (not_1_out, clock_1_out);
  not not_2 (not_2_out, not_1_out);
  not not_3 (not_3_out, Input);
  and and_1 (and_1_out, clock_1_out, not_4_out);
  not not_4 (not_4_out, not_2_out);
  and and_2 (and_2_out, not_3_out, Enable);
  and and_3 (and_3_out, Enable, Input);
  and and_4 (and_4_out, and_1_out, Enable_2);
  nor nor_3 (Output, and_2_out, nor_4_out);
  nor nor_4 (nor_4_out, Output, and_3_out);
  not not_5 (not_5_out, Input_3);
  and and_5 (and_5_out, not_5_out, and_4_out);
  and and_6 (and_6_out, and_4_out, Input_3);
  nor nor_5 (Output_3, and_5_out, nor_6_out);
  nor nor_6 (nor_6_out, Output_3, and_6_out);

  // Notes on the sheet:
  //   Reset
  //   A Simple Latch
  //   A simple latch remembers if the input was 1
  //   S-R Latch
  //   - similar to D-latch but 'reset' sets both outputs to 0
  //   if input is 0 or sets output to 1 if inp was 1
  //   Latches
  //   - root of remebering input of values
  //   Clock
  //   when it gets witten to output)
  //   (Click 'Simulate' and check Ticks Enabled, set Enabled to 1, then switch Input values to see
  //   D Latch
  //   - When enable is turned on, output reflects input value 
  //   else, when enable is off, output remains in the last set value
  //   and doesn't get affected by the input value
  //   D Flip Flop
  //   - D-Flip-Flop when enable is turned on, writes input value to output only at the rising edge of the clock
endmodule
