// Logisim project kan_subtractor.circ as structural Verilog: 1 circuit, main circuit main
module main (
  input  in_1,
  input  A,
  input  B,
  input  in_4,
  input  A_2,
  input  B_2,
  output Result,
  output out_8,
  output Result_2,
  output out_10
);

  wire and_1_out, and_2_out, not_1_out, not_2_out, not_3_out, xor_1_out;

  not not_1 (not_1_out, A_2);
  Subtractor #(.width(1)) subtractor_1 (.a(A), .b(B), .out(Result), .bin(in_1), .bout(out_8));
  xor xor_1 (xor_1_out, B_2, in_4);
  not not_2 (not_2_out, xor_1_out);
  Adder #(.width(1)) adder_1 (.a(A_2), .b(xor_1_out), .out(Result_2), .cin(in_4));  // open: cout
  not not_3 (not_3_out, Result_2);
  and and_1 (and_1_out, not_3_out, xor_1_out, A_2);
  and and_2 (and_2_out, Result_2, not_2_out, not_1_out);
  or or_1 (out_10, and_1_out, and_2_out);

  // Notes on the sheet:
  //   Logisim's built-in subtractor
  //   My implementation of the subtractor using full-adder, 'and', 'or', 'xor', 'not' gates
  //   Indicates whether result is negative
  //   Subtractor
  //   A - B
  //   = A + (~B) +1
  //   Performs addition when turned off else subtraction
  //   Indicates whether result is negative
  //   - Performs binary subtraction
  //   - A and B are input values, which can be 0 or 1
endmodule
